# Fritzing sketch Dtoy_sketch (saved by Fritzing 0.9.2b)
breadboards: 1

parts:
  Part1 = Arduino Nano (Rev3.0)
  LED1 = LED - 5mm [color="Red (633nm)" package="5 mm [THT]"]
  LED2 = LED - 5mm [color="Red (633nm)" package="5 mm [THT]"]
  R1 = Resistor [tolerance=±5% resistance=220 package=THT]
  R2 = Resistor [tolerance=±5% resistance=220 package=THT]
  PIR1 = PIR sensor

nets:
  N1: Part1.D2, PIR1.SIG
  N2: Part1.D3, R1.Pin_0
  N3: Part1.D5, R2.Pin_0
  GND: Part1.GND, LED1.cathode, LED2.cathode, PIR1.GND
  5V: Part1.5V, PIR1.VDD
  N4: LED1.anode, R1.Pin_1
  N5: LED2.anode, R2.Pin_1
